# Fritzing sketch SimplePotControl (saved by Fritzing 0.9.10b)
breadboards: 1

parts:
  R1 = Rotary Potentiometer (Small) [maximum_resistance=100kΩ knob_status=50% power=0.5W package=THT]
  Part1 = Arduino Uno (Rev3) - ICSP
  JP1 = Header 6 [package=molex-1x6_lock]

nets:
  N1: R1.leg1, Part1.3V3
  N2: R1.wiper, Part1.A0
  N3: R1.leg2, Part1.GND, JP1.3
  N4: Part1.ICSP_MOSI, Part1.D11_PWM/MOSI, JP1.2
  N5: Part1.D10_PWM/SS, JP1.1
  N6: Part1.D12/MISO, JP1.6
  N7: Part1.D13/SCK, JP1.4

notes:
  1 - nCS/10
  2 - COPI/11
  3 - GND/GND
  4 - CLK/13
  5 - PWR/NA
  6 - CIPO/12
