# Fritzing sketch AudioMessage (saved by Fritzing 0.9.10b)
breadboards: 2

parts:
  DFRobot_DFPlayer_Mini1 = DFRobot DFPlayer Mini [part_number=DFR0299]
  U1 = ESP32-38PinWide [part_number=ESP32-38PinWide]
  AMP1 = GF1002 Stereo Amplifier
  S1 = Pushbutton [package="[THT]"]
  S2 = Pushbutton [package="[THT]"]
  S3 = Pushbutton [package="[THT]"]
  R1 = Resistor [tolerance=±5% power=0.25 resistance=220 package=THT]
  R2 = Resistor [tolerance=±5% power=0.25 resistance=220 package=THT]
  R3 = Resistor [tolerance=±5% power=0.25 resistance=220 package=THT]
  R4 = Resistor [tolerance=±5% power=0.25 resistance=220 package=THT]
  SP1 = SPEAKER [package=pcb_mount_speaker]
  LCM1602_IIC1 = LCM1602 IIC [part_number="LCM1602 IIC" chip_label="LCM1602 IIC" package="DIP (Dual Inline) [THT]"]
  LCD1 = LCD screen

nets:
  VCC: DFRobot_DFPlayer_Mini1.VCC, DFRobot_DFPlayer_Mini1.TX, U1.VIN, U1.GPIO16, AMP1.POWER+, R4.Pin_1, LCM1602_IIC1.VCC
  N1: DFRobot_DFPlayer_Mini1.DAC_R, AMP1.INPUTR
  N2: DFRobot_DFPlayer_Mini1.DAC_L, AMP1.INPUTL
  GND: DFRobot_DFPlayer_Mini1.GND-1, DFRobot_DFPlayer_Mini1.GND-2, U1.GND, AMP1.POWER-, AMP1.INPUTG, R4.Pin_0, LCM1602_IIC1.GND
  N3: U1.3.3, R1.Pin_1, R2.Pin_1, R3.Pin_1
  N4: U1.GPIO34, S3.Pin_1, S3.Pin_2, R1.Pin_0
  N5: U1.GPIO33, S1.Pin_1, S1.Pin_2, R2.Pin_0
  N6: U1.GPIO14, S2.Pin_1, S2.Pin_2, R3.Pin_0
  N7: U1.GPIO11, S1.Pin_3, S1.Pin_4, S2.Pin_3, S2.Pin_4, S3.Pin_3, S3.Pin_4
  N8: AMP1.LOUT+, SP1.-
  N9: AMP1.LOUT-, SP1.+
  VSS: LCM1602_IIC1.VSS, LCD1.VSS
  VDD: LCM1602_IIC1.VDD, LCD1.VDD
  N10: LCM1602_IIC1.V0, LCD1.V0
  N11: LCM1602_IIC1.RS, LCD1.RS
  N12: LCM1602_IIC1.RW, LCD1.R/W
  N13: LCM1602_IIC1.E, LCD1.E
  N14: LCM1602_IIC1.D0, LCD1.DB0
  N15: LCM1602_IIC1.D1, LCD1.DB1
  N16: LCM1602_IIC1.D2, LCD1.DB2
  N17: LCM1602_IIC1.D3, LCD1.DB3
  N18: LCM1602_IIC1.D4, LCD1.DB4
  N19: LCM1602_IIC1.D5, LCD1.DB5
  N20: LCM1602_IIC1.D6, LCD1.DB6
  N21: LCM1602_IIC1.D7, LCD1.DB7
  N22: LCM1602_IIC1.A, LCD1.LED+
  N23: LCM1602_IIC1.K, LCD1.LED-

notes:
  R = 10k ohms

custom parts:
  ESP32-38PinWide: Generic 38-Pin ESP32 with wide format (only access to one side of pins on a breadboard) based on Stephen Lilley's HiLetgo ESP-WROOM-32 ESP32 ESP-32S Development Board.
  GF1002 Stereo Amplifier: GF1002 6 Watt Stereo Amplifier
  LCM1602 IIC: I2C-Module to use a 1602 or 2004 LCD on with the wire.h libory Serial LCD Modul
